# Fritzing sketch electron-gps (saved by Fritzing 0.9.2b)
breadboards: 1

parts:
  Photon = Photon
  GPS1 = Adafruit Ultimate GPS Breakout  # not connected
  R1 = Resistor [tolerance=±10% resistance=2.2k package=THT]

nets:
  N1: Photon.GND, R1.Pin_1
  N2: Photon.D4, R1.Pin_0
